# Fritzing sketch leds (saved by Fritzing 0.9.2b)
breadboards: 1

parts:
  Raspberry_Pi1 = Raspberry Pi 2
  R1 = Resistor [tolerance=±5% resistance=220 package=THT]
  R2 = Resistor [tolerance=±5% resistance=220 package=THT]
  R3 = Resistor [tolerance=±5% resistance=220 package=THT]
  R4 = Resistor [tolerance=±5% resistance=220 package=THT]
  LED1 = LED - 5mm [color="Green (565nm)" package="5 mm [THT]"]
  LED2 = LED - 5mm [color="Blue (430nm)" package="5 mm [THT]"]
  LED3 = LED - 5mm [color="Yellow (585nm)" package="5 mm [THT]"]
  LED4 = LED - 5mm [color="Red (633nm)" package="5 mm [THT]"]

nets:
  N1: Raspberry_Pi1.GPIO4, LED1.anode
  N2: Raspberry_Pi1.GPIO17, LED2.anode
  N3: Raspberry_Pi1.GPIO22, LED3.anode
  N4: Raspberry_Pi1.GPIO5, LED4.anode
  N5: Raspberry_Pi1.GND, R1.Pin_1, R2.Pin_1, R3.Pin_1, R4.Pin_1
  N6: R1.Pin_0, LED2.cathode
  N7: R2.Pin_0, LED3.cathode
  N8: R3.Pin_0, LED4.cathode
  N9: R4.Pin_0, LED1.cathode
